# Fritzing sketch leonardo-ir (saved by Fritzing 0.9.6b)
breadboards: 1

parts:
  Part1 = Arduino Leonardo (Rev3b)
  LED1 = LED - 5mm [color="Green (565nm)" current=0.030 package="5 mm [THT]"]
  Q1 = NPN-Transistor [package="TO92 [THT]"]
  LED2 = LED - 5mm [color="Infrared (850nm)" current=0.030 package="5 mm [THT]"]
  LED3 = LED - 5mm [color="Infrared (850nm)" current=0.030 package="5 mm [THT]"]

nets (from the breadboard view):
  N1: Part1.5V, LED2.anode, LED3.anode
  N2: Part1.D9_PWM/A9, LED1.anode
  N3: Part1.GND, Q1.C
  N4: LED1.cathode, Q1.B
  N5: Q1.E, LED2.cathode, LED3.cathode
