# Fritzing sketch nano-ir (saved by Fritzing 0.9.2b)
breadboards: 1

parts:
  Q1 = NPN-Transistor [package="TO92 [THT]"]
  LED1 = LED - 5mm [color="Green (565nm)" package="5 mm [THT]"]
  LED2 = LED - 5mm [color="Infrared (850nm)" package="5 mm [THT]"]
  LED3 = LED - 5mm [color="Infrared (850nm)" package="5 mm [THT]"]
  part = NPN-Transistor [package="TO92 [THT]"]  # not connected
  Part1 = Arduino Nano (Rev3.0)

nets:
  N1: Q1.E, LED2.cathode, LED3.cathode
  N2: Q1.B, LED1.anode
  N3: Q1.C, Part1.GND
  N4: LED1.cathode, Part1.D3
  N5: LED2.anode, LED3.anode, Part1.VIN
